// Logisim project alu.circ as structural Verilog: 2 circuits, main circuit main
module main (
  input  [31:0] X,
  input  [31:0] Y,
  input  [5:0] Switch__S,
  output Signed_Overflow,
  output [31:0] RESULT,
  output Equal
);

  wire bout1, bout2, comparator_2_eq, comparator_3_eq, comparator_4_lt, comparator_5_lt, comparator_6_eq,
       cout1, cout2, signedadd, signedsub, xor_1_out, xor_2_out;
  wire [4:0] bit_extender_1_out, bit_extender_2_out, bit_extender_3_out;
  wire [31:0] add, addu, \and , bitpal, lfsr, multiplexer_1_out, multiplexer_3_out, \or , shift_result, sll,
       slt, sltu, sra, srl, sub, subu;

  Comparator #(.width(32)) comparator_1 (.a(X), .b(Y), .eq(Equal));  // open: gt, lt
  Bit_Extender #(.in_width(32), .out_width(5)) bit_extender_1 (.in(Y), .out(bit_extender_1_out));
  Bit_Extender #(.in_width(32), .out_width(5)) bit_extender_2 (.in(Y), .out(bit_extender_2_out));
  Bit_Extender #(.in_width(32), .out_width(5)) bit_extender_3 (.in(Y), .out(bit_extender_3_out));
  Adder #(.width(31)) adder_1 (.a(X[30:0]), .b(Y[30:0]), .out(add[30:0]), .cout(cout1));  // open: cin
  Comparator #(.width(6)) comparator_2 (.a(Switch__S), .b(6'b100000), .eq(comparator_2_eq));  // open: gt, lt
  xor xor_1 (xor_1_out, cout1, cout2);
  Subtractor #(.width(31)) subtractor_1 (.a(X[30:0]), .b(Y[30:0]), .out(sub[30:0]), .bout(bout1));  // open: bin
  Comparator #(.width(6)) comparator_3 (.a(Switch__S), .b(6'b100010), .eq(comparator_3_eq));  // open: gt, lt
  xor xor_2 (xor_2_out, bout1, bout2);
  Adder #(.width(32)) adder_2 (.a(X), .b(Y), .out(addu));  // open: cin, cout
  Subtractor #(.width(32)) subtractor_2 (.a(X), .b(Y), .out(subu));  // open: bin, bout
  assign \and  = X & Y;  // AND_Gate and_1, 32 bits wide
  assign \or  = X | Y;  // OR_Gate or_1, 32 bits wide
  Comparator #(.width(32)) comparator_4 (.a(X), .b(Y), .lt(comparator_4_lt));  // open: gt, eq
  Comparator #(.width(32)) comparator_5 (.a(X), .b(Y), .lt(comparator_5_lt));  // open: gt, eq
  Comparator #(.width(16)) comparator_6 (
    .a(X[15:0]),
    .b({X[16], X[17], X[18], X[19], X[20], X[21], X[22], X[23], X[24], X[25], X[26], X[27], X[28], X[29], X[30], X[31]}),
    .eq(comparator_6_eq));  // open: gt, lt
  Shifter #(.width(32), .shift("lr")) shifter_1 (.in(X), .\dist (5'b00001), .out(shift_result));
  Bit_Extender #(.in_width(32), .out_width(31)) bit_extender_4 (.in(shift_result), .out(lfsr[30:0]));
  Shifter #(.width(32)) shifter_2 (.in(X), .\dist (bit_extender_1_out), .out(sll));
  Shifter #(.width(32), .shift("lr")) shifter_3 (.in(X), .\dist (bit_extender_2_out), .out(srl));
  Shifter #(.width(32), .shift("ar")) shifter_4 (.in(X), .\dist (bit_extender_3_out), .out(sra));
  Adder #(.width(1)) adder_3 (.a(X[31]), .b(Y[31]), .out(add[31]), .cin(cout1), .cout(cout2));
  and and_2 (signedadd, comparator_2_eq, xor_1_out);
  Subtractor #(.width(1)) subtractor_3 (.a(X[31]), .b(Y[31]), .out(sub[31]), .bin(bout1), .bout(bout2));
  and and_3 (signedsub, comparator_3_eq, xor_2_out);
  assign slt = {{31{1'b0}}, comparator_4_lt};  // Bit_Extender bit_extender_5
  assign sltu = {{31{1'b0}}, comparator_5_lt};  // Bit_Extender bit_extender_6
  assign bitpal = {{31{1'b0}}, comparator_6_eq};  // Bit_Extender bit_extender_7
  ExactlyOne xor_3 (.out(lfsr[31]), .in0(X[0]), .in1(X[2]), .in2(X[3]), .in3(X[5]));
  Multiplexer #(.select(5), .width(32), .enable("false")) multiplexer_1 (
    .in0(sll), .in3(srl), .in6(sra), .in9(add), .in12(addu), .in15(sub), .in18(subu), .in21(\and ),
    .in24(\or ), .in27(slt), .in30(sltu), .out(multiplexer_1_out), .sel(Switch__S[4:0]));  // open: in1, in2, in4, in5, in7, in8, in10, in11, in13, in14, in16, in17, in19, in20, in22, in23, in25, in26, in28, in29, in31
  Multiplexer #(.width(32), .enable("false")) multiplexer_2 (
    .in0(multiplexer_1_out), .in1(multiplexer_3_out), .out(RESULT), .sel(Switch__S[5]));
  Multiplexer #(.select(5), .width(32), .enable("false")) multiplexer_3 (
    .in27(bitpal), .in30(lfsr), .out(multiplexer_3_out), .sel(Switch__S[4:0]));  // open: in0, in1, in2, in3, in4, in5, in6, in7, in8, in9, in10, in11, in12, in13, in14, in15, in16, in17, in18, in19, in20, in21, in22, in23, in24, in25, in26, in28, in29, in31
  or or_2 (Signed_Overflow, signedadd, signedsub);

  // Other names for the same wires on the sheet: xinput[31:0] = X; xor_result = lfsr[31]; signed = Signed_Overflow;
  //   control5[4:0] = Switch__S[4:0]; switch[5:0] = Switch__S; control1 = Switch__S[5]; yinput[31:0] = Y

  // Notes on the sheet:
  //   INPUTS to your circuit
  //   INPUT to your circuit
  //   DON'T CHANGE THE INPUTS AND OUTPUTS! IF YOU DO SO, YOU NEED TO MAKE SURE THE PINS ARE IN THE RIGHT PLACES!
  //   OUTPUTS of your circuit
endmodule

module lfsr (
  input  [31:0] X,
  output [31:0] RESULT
);

  wire [31:0] shift_result;

  Shifter #(.width(32), .shift("lr")) shifter_1 (.in(X), .\dist (5'b00001), .out(shift_result));
  ExactlyOne xor_1 (.out(RESULT[31]), .in0(X[0]), .in1(X[2]), .in2(X[3]), .in3(X[5]));
  Bit_Extender #(.in_width(32), .out_width(31)) bit_extender_1 (.in(shift_result), .out(RESULT[30:0]));

  // Other names for the same wires on the sheet: xor_result = RESULT[31]

  // Notes on the sheet:
  //   OUTPUTS of your circuit
endmodule
