// Logisim project cpu.circ as structural Verilog: 2 circuits, main circuit main
module main (
  input  [31:0] RS_READ_VALUE,
  input  [31:0] RT_READ_VALUE,
  input  [31:0] INSTRUCTION,
  input  CLOCK,
  input  RESET,
  output [31:0] t0,
  output [31:0] t1,
  output [31:0] t2,
  output [31:0] t3,
  output [4:0] RS,
  output [4:0] RT,
  output [4:0] Write_Register,
  output [31:0] RD_WRITE_VALUE,
  output RD_WRITE_ENABLE,
  output [23:0] FETCH_ADDRESS
);

  wire accessByte, ALU_signed_overflow, ALUEqual, ExtOp, j, jal, jr, jump, lui, MemtoReg, MemWr, nPC_sel,
       or_1_out, or_2_out, or_3_out, or_4_out, RegDst, t__RegWr, use__t__rd, use__t__rs, use__t__rt;
  wire [1:0] aluSrc, t__writeRegister;
  wire [4:0] multiplexer_13_out;
  wire [5:0] ALUCtr;
  wire [23:0] adder_1_out, adder_2_out, adder_3_out, bit_extender_1_out, bit_extender_2_out,
       bit_extender_3_out, fetchAddrAfter, multiplexer_4_out, multiplexer_6_out, PCaddr, subtractor_1_out,
       subtractor_2_out, subtractor_3_out;
  wire [31:0] afterPipe, alu_input_1, alu_input_2, aluOutput, bit_extender_4_out, bit_extender_5_out,
       bit_extender_6_out, bit_extender_7_out, data_after_memory, data_in, extended, MEM_data_mem_out,
       multiplexer_1_out, multiplexer_3_out, multiplexer_9_out, multiplexer_16_out, shifter_1_out,
       shifter_2_out, t__writeRegVal, t_rs_read, t_rt_read;

  or or_1 (or_1_out, nPC_sel, jump);
  Multiplexer #(.width(32), .enable("false")) multiplexer_1 (
    .in0(INSTRUCTION), .in1({32{1'b0}}), .out(multiplexer_1_out), .sel(or_1_out));
  Register #(.width(24)) register_1 (.D(PCaddr), .Q(fetchAddrAfter), .clk(CLOCK));  // open: en, clr
  Subtractor #(.width(24)) subtractor_1 (.a(fetchAddrAfter), .b(24'h1), .out(subtractor_1_out));  // open: bin, bout
  Register #(.width(32)) register_2 (
    .D(multiplexer_1_out), .en(1'b1), .Q({afterPipe[31:26], RS, RT, afterPipe[15:0]}), .clk(CLOCK));  // open: clr
  Multiplexer #(.width(24)) multiplexer_2 (
    .in0(fetchAddrAfter), .in1(subtractor_1_out), .out(FETCH_ADDRESS), .sel(or_2_out));  // open: en
  or or_2 (or_2_out, nPC_sel, jump);
  // Probe on {afterPipe[31:26], RS, RT, afterPipe[15:0]}
  // Probe on afterPipe[15:0]
  Multiplexer #(.width(32)) multiplexer_3 (
    .in0(RS_READ_VALUE), .in1(t_rs_read), .out(multiplexer_3_out), .sel(use__t__rs));  // open: en
  // Probe on {RS, RT, afterPipe[15:0]}
  Bit_Extender #(.in_width(32), .out_width(24)) bit_extender_1 (.in(multiplexer_3_out), .out(bit_extender_1_out));
  Adder #(.width(24)) adder_1 (.a(FETCH_ADDRESS), .b(24'h1), .out(adder_1_out));  // open: cin, cout
  assign bit_extender_2_out = {{8{afterPipe[15]}}, afterPipe[15:0]};  // Bit_Extender bit_extender_2
  Bit_Extender #(.in_width(26), .out_width(24)) bit_extender_3 (
    .in({RS, RT, afterPipe[15:0]}), .out(bit_extender_3_out));
  Subtractor #(.width(24)) subtractor_2 (
    .a(bit_extender_3_out), .b(24'h100000), .out(subtractor_2_out));  // open: bin, bout
  Subtractor #(.width(24)) subtractor_3 (
    .a(bit_extender_1_out), .b(24'h100000), .out(subtractor_3_out));  // open: bin, bout
  Adder #(.width(24)) adder_2 (.a(adder_1_out), .b(bit_extender_2_out), .out(adder_2_out));  // open: cin, cout
  Multiplexer #(.width(24), .enable("false")) multiplexer_4 (
    .in0(multiplexer_6_out), .in1(subtractor_2_out), .out(multiplexer_4_out), .sel(or_3_out));
  or or_3 (or_3_out, j, jal);
  Multiplexer #(.width(24), .enable("false")) multiplexer_5 (
    .in0(multiplexer_4_out), .in1(subtractor_3_out), .out(PCaddr), .sel(jr));
  Multiplexer #(.width(24), .enable("false")) multiplexer_6 (
    .in0(adder_1_out), .in1(adder_2_out), .out(multiplexer_6_out), .sel(nPC_sel));
  Comparator #(.width(3)) comparator_1 (.a(RT[4:2]), .b(3'b010), .eq(use__t__rt));  // open: gt, lt
  Comparator #(.width(3)) comparator_2 (.a(RS[4:2]), .b(3'b010), .eq(use__t__rs));  // open: gt, lt
  Comparator #(.width(3)) comparator_3 (.a(afterPipe[15:13]), .b(3'b010), .eq(use__t__rd));  // open: gt, lt
  or or_4 (or_4_out, use__t__rt, use__t__rd);
  control control (
    .INSTRUCTION({afterPipe[31:26], RS, RT, afterPipe[15:0]}), .ALUEqual(ALUEqual), .nPC_sel(nPC_sel),
    .RegDst(RegDst), .RegWr(RD_WRITE_ENABLE), .ExtOp(ExtOp), .ALUSrc(aluSrc), .ALUCtr(ALUCtr), .MemWr(MemWr),
    .MemtoReg(MemtoReg), .Jump(jump), .AccessByte(accessByte), .lui(lui), .j(j), .jal(jal), .jr(jr));
  regfile_main RegFile (
    .Read_register_1(RS[1:0]), .Read_register_2(RT[1:0]), .write_register(t__writeRegister),
    .write_data(t__writeRegVal), .t0_Value(t0), .t1_Value(t1), .t2_Value(t2), .t3_Value(t3),
    .RegWrite(t__RegWr), .clock(CLOCK), .Read_Data_1(t_rs_read), .Read_Data_2(t_rt_read));
  and and_1 (t__RegWr, or_4_out, RD_WRITE_ENABLE);
  assign bit_extender_4_out = {{16{1'b0}}, afterPipe[15:0]};  // Bit_Extender bit_extender_4
  assign bit_extender_5_out = {{16{afterPipe[15]}}, afterPipe[15:0]};  // Bit_Extender bit_extender_5
  Multiplexer #(.width(32), .enable("false")) multiplexer_7 (
    .in0(bit_extender_4_out), .in1(bit_extender_5_out), .out(extended), .sel(ExtOp));
  // Probe on alu_input_1
  Multiplexer #(.width(32)) multiplexer_8 (
    .in0(RS_READ_VALUE), .in1(t_rs_read), .out(alu_input_1), .sel(use__t__rs));  // open: en
  LED led_1 (.in(ALU_signed_overflow));
  alu_main ALU (
    .Switch__S(ALUCtr), .X(alu_input_1), .Equal(ALUEqual), .RESULT(aluOutput),
    .Signed_Overflow(ALU_signed_overflow), .Y(alu_input_2));
  Multiplexer #(.width(32)) multiplexer_9 (
    .in0(RT_READ_VALUE), .in1(t_rt_read), .out(multiplexer_9_out), .sel(use__t__rt));  // open: en
  assign bit_extender_6_out = {{27{1'b0}}, afterPipe[10:6]};  // Bit_Extender bit_extender_6
  // Probe on aluOutput
  // Probe on alu_input_2
  Multiplexer #(.select(2), .width(32)) multiplexer_10 (
    .in0(multiplexer_9_out), .in1(extended), .in2(bit_extender_6_out), .out(alu_input_2), .sel(aluSrc));  // open: in3, en
  // Probe on data_in
  Multiplexer #(.width(32)) multiplexer_11 (
    .in0(RT_READ_VALUE), .in1(t_rt_read), .out(data_in), .sel(use__t__rt));  // open: en
  mem_main MEM (
    .Data_Mem_Addr(aluOutput), .Data_Mem_In(data_in), .ACCESS_BYTE(accessByte), .MEM_WRITE(MemWr),
    .CLOCK(CLOCK), .Data_Mem_Out(MEM_data_mem_out));
  Multiplexer #(.width(32), .enable("false")) multiplexer_12 (
    .in0(aluOutput), .in1(MEM_data_mem_out), .out(data_after_memory), .sel(MemtoReg));
  Adder #(.width(24)) adder_3 (.a(FETCH_ADDRESS), .b(24'h100001), .out(adder_3_out));  // open: cin, cout
  Multiplexer #(.width(5)) multiplexer_13 (
    .in0(RT), .in1(afterPipe[15:11]), .out(multiplexer_13_out), .sel(RegDst));  // open: en
  assign bit_extender_7_out = {{8{1'b0}}, adder_3_out};  // Bit_Extender bit_extender_7
  Multiplexer #(.width(5), .enable("false")) multiplexer_14 (
    .in0(multiplexer_13_out), .in1({5{1'b1}}), .out(Write_Register), .sel(jal));
  Shifter #(.width(32)) shifter_1 (.in(extended), .\dist (5'b10000), .out(shifter_1_out));
  Multiplexer #(.width(2)) multiplexer_15 (
    .in0(RT[1:0]), .in1(afterPipe[12:11]), .out(t__writeRegister), .sel(RegDst));  // open: en
  Multiplexer #(.width(32), .enable("false")) multiplexer_16 (
    .in0(data_after_memory), .in1(bit_extender_7_out), .out(multiplexer_16_out), .sel(jal));
  Multiplexer #(.width(32), .enable("false")) multiplexer_17 (
    .in0(data_after_memory), .in1(shifter_1_out), .out(t__writeRegVal), .sel(lui));
  Shifter #(.width(32)) shifter_2 (.in(extended), .\dist (5'b10000), .out(shifter_2_out));
  Multiplexer #(.width(32), .enable("false")) multiplexer_18 (
    .in0(multiplexer_16_out), .in1(shifter_2_out), .out(RD_WRITE_VALUE), .sel(lui));
  // Probe on RD_WRITE_VALUE

  // Other names for the same wires on the sheet: opcode[5:0] = afterPipe[31:26]; fetchAddr[23:0] = FETCH_ADDRESS;
  //   funct[5:0] = afterPipe[5:0]; immediate[15:0] = afterPipe[15:0]; jumpAddr[25:0] = {RS, RT, afterPipe[15:0]};
  //   shamt[4:0] = afterPipe[10:6]; rd[4:0] = afterPipe[15:11]; t__input__rd[1:0] = afterPipe[12:11];
  //   afterPipe[25:16] = {RS, RT}; t__input__rt[1:0] = RT[1:0]; t__input__rs[1:0] = RS[1:0]; RegWr = RD_WRITE_ENABLE;
  //   rs_read[31:0] = RS_READ_VALUE; rt_read[31:0] = RT_READ_VALUE; writeRegister[4:0] = Write_Register;
  //   writeRegVal[31:0] = RD_WRITE_VALUE

  // Notes on the sheet:
  //   These are outputs/inputs from run.circ
  //   These are outputs to run.circ
  //   Step 1: Instruction Fetch & PC Addressing
  //   PC Addressing
  //   Step 2: read register
  //   Step 3: execute
  //   Step 4: Memory
  //   Fig 3: memory
  //   Step 5: Write back to register
  //   jal - write to $ra
endmodule

module control (
  input  [31:0] INSTRUCTION,
  input  ALUEqual,
  output nPC_sel,
  output RegDst,
  output RegWr,
  output ExtOp,
  output [1:0] ALUSrc,
  output [5:0] ALUCtr,
  output MemWr,
  output MemtoReg,
  output Jump,
  output AccessByte,
  output lui,
  output j,
  output jal,
  output jr
);

  wire addiu, and_2_out, and_3_out, and_4_out, and_5_out, andi, beq, bne, comparator_13_eq, comparator_14_eq,
       comparator_15_eq, comparator_16_eq, comparator_17_eq, comparator_18_eq, comparator_19_eq,
       comparator_20_eq, comparator_21_eq, comparator_22_eq, comparator_23_eq, comparator_24_eq,
       comparator_25_eq, lb, lbu, lw, not_1_out, not_2_out, or_1_out, or_2_out, or_3_out, or_4_out, or_5_out,
       or_6_out, or_7_out, or_8_out, or_9_out, or_10_out, or_11_out, ori;
  wire [5:0] otherInstructions;

  Comparator #(.width(6)) comparator_1 (.a(6'b001001), .b(INSTRUCTION[31:26]), .eq(addiu));  // open: gt, lt
  Comparator #(.width(6)) comparator_2 (.a(6'b001100), .b(INSTRUCTION[31:26]), .eq(andi));  // open: gt, lt
  Comparator #(.width(6)) comparator_3 (.a(6'b001101), .b(INSTRUCTION[31:26]), .eq(ori));  // open: gt, lt
  Comparator #(.width(6)) comparator_4 (.a(INSTRUCTION[31:26]), .b(6'b001111), .eq(lui));  // open: gt, lt
  Comparator #(.width(6)) comparator_5 (.a(6'b100000), .b(INSTRUCTION[31:26]), .eq(lb));  // open: gt, lt
  Comparator #(.width(6)) comparator_6 (.a(6'b100100), .b(INSTRUCTION[31:26]), .eq(lbu));  // open: gt, lt
  Comparator #(.width(6)) comparator_7 (.a(6'b100011), .b(INSTRUCTION[31:26]), .eq(lw));  // open: gt, lt
  Comparator #(.width(6)) comparator_8 (.a(6'b101011), .b(INSTRUCTION[31:26]), .eq(MemWr));  // open: gt, lt
  Comparator #(.width(6)) comparator_9 (.a(6'b000100), .b(INSTRUCTION[31:26]), .eq(beq));  // open: gt, lt
  Comparator #(.width(6)) comparator_10 (.a(6'b000101), .b(INSTRUCTION[31:26]), .eq(bne));  // open: gt, lt
  Comparator #(.width(6)) comparator_11 (.a(6'b000011), .b(INSTRUCTION[31:26]), .eq(jal));  // open: gt, lt
  Comparator #(.width(6)) comparator_12 (.a(6'b000010), .b(INSTRUCTION[31:26]), .eq(j));  // open: gt, lt
  Comparator #(.width(6)) comparator_13 (.a({6{1'b0}}), .b(INSTRUCTION[31:26]), .eq(comparator_13_eq));  // open: gt, lt
  and and_1 (jr, comparator_13_eq, comparator_14_eq);
  Comparator #(.width(6)) comparator_14 (.a(6'b001000), .b(INSTRUCTION[5:0]), .eq(comparator_14_eq));  // open: gt, lt
  Comparator #(.width(6)) comparator_15 (.a(INSTRUCTION[5:0]), .b(6'b000010), .eq(comparator_15_eq));  // open: gt, lt
  Comparator #(.width(6)) comparator_16 (.a(INSTRUCTION[5:0]), .b({6{1'b0}}), .eq(comparator_16_eq));  // open: gt, lt
  Comparator #(.width(6)) comparator_17 (.a(INSTRUCTION[5:0]), .b(6'b000011), .eq(comparator_17_eq));  // open: gt, lt
  Multiplexer multiplexer_1 (.in0(1'b0), .in1(1'b1), .out(RegDst), .sel(comparator_18_eq));  // open: en
  Comparator #(.width(6)) comparator_18 (.a(INSTRUCTION[31:26]), .b({6{1'b0}}), .eq(comparator_18_eq));  // open: gt, lt
  Comparator #(.width(6)) comparator_19 (.a(INSTRUCTION[31:26]), .b({6{1'b0}}), .eq(comparator_19_eq));  // open: gt, lt
  Multiplexer multiplexer_2 (.in0(1'b0), .in1(1'b1), .out(ExtOp), .sel(or_1_out));  // open: en
  or or_1 (or_1_out, addiu, lw, MemWr, lb, lbu);
  or or_2 (or_2_out, comparator_15_eq, comparator_16_eq, comparator_17_eq);
  or or_3 (or_3_out, addiu, andi, ori, lui, lb, lbu, lw, MemWr);
  or or_4 (or_4_out, addiu, andi, ori, lui, jal, lb, lbu, lw, comparator_19_eq);
  Comparator #(.width(6)) comparator_20 (.a(INSTRUCTION[31:26]), .b({6{1'b0}}), .eq(comparator_20_eq));  // open: gt, lt
  not not_1 (not_1_out, or_2_out);
  assign ALUSrc = or_3_out ? 2'b01 : 2'bz;  // Controlled_Buffer imm
  Multiplexer multiplexer_3 (.in0(1'b0), .in1(1'b1), .out(RegWr), .sel(or_4_out));  // open: en
  assign ALUSrc = or_5_out ? 2'b00 : 2'bz;  // Controlled_Buffer reg
  and and_2 (and_2_out, comparator_20_eq, not_1_out);
  or or_5 (or_5_out, and_2_out, bne, beq);
  assign otherInstructions = andi ? 6'b100100 : 6'bz;  // Controlled_Buffer controlled_buffer_1
  assign otherInstructions = ori ? 6'b100101 : 6'bz;  // Controlled_Buffer controlled_buffer_2
  assign otherInstructions = lui ? {6{1'b0}} : 6'bz;  // Controlled_Buffer controlled_buffer_3
  Comparator #(.width(6)) comparator_21 (.a(INSTRUCTION[5:0]), .b(6'b000010), .eq(comparator_21_eq));  // open: gt, lt
  Comparator #(.width(6)) comparator_22 (.a(INSTRUCTION[5:0]), .b({6{1'b0}}), .eq(comparator_22_eq));  // open: gt, lt
  Comparator #(.width(6)) comparator_23 (.a(INSTRUCTION[5:0]), .b(6'b000011), .eq(comparator_23_eq));  // open: gt, lt
  Comparator #(.width(6)) comparator_24 (.a(INSTRUCTION[31:26]), .b({6{1'b0}}), .eq(comparator_24_eq));  // open: gt, lt
  assign otherInstructions = addiu ? 6'b100001 : 6'bz;  // Controlled_Buffer controlled_buffer_4
  assign otherInstructions = or_6_out ? 6'b100000 : 6'bz;  // Controlled_Buffer controlled_buffer_5
  or or_6 (or_6_out, lb, lw, MemWr, lbu);
  Multiplexer #(.width(6), .enable("false")) multiplexer_4 (
    .in0(otherInstructions), .in1(INSTRUCTION[5:0]), .out(ALUCtr), .sel(comparator_25_eq));
  Comparator #(.width(6)) comparator_25 (.a(INSTRUCTION[31:26]), .b({6{1'b0}}), .eq(comparator_25_eq));  // open: gt, lt
  assign ALUSrc = and_3_out ? 2'b10 : 2'bz;  // Controlled_Buffer shamt
  or or_7 (or_7_out, comparator_21_eq, comparator_22_eq, comparator_23_eq);
  and and_3 (and_3_out, or_7_out, comparator_24_eq);
  Multiplexer multiplexer_5 (.in0(1'b0), .in1(1'b1), .out(MemtoReg), .sel(or_8_out));  // open: en
  or or_8 (or_8_out, lb, lbu, lw);
  and and_4 (and_4_out, beq, ALUEqual);
  not not_2 (not_2_out, ALUEqual);
  and and_5 (and_5_out, not_2_out, bne);
  Multiplexer #(.enable("false")) multiplexer_6 (.in0(1'b0), .in1(1'b1), .out(AccessByte), .sel(or_9_out));
  or or_9 (or_9_out, lb, lbu);
  Multiplexer #(.enable("false")) multiplexer_7 (.in0(1'b0), .in1(1'b1), .out(Jump), .sel(or_10_out));
  or or_10 (or_10_out, j, jr, jal);
  or or_11 (or_11_out, and_4_out, and_5_out);
  Multiplexer multiplexer_8 (.in0(1'b0), .in1(1'b1), .out(nPC_sel), .sel(or_11_out));  // open: en

  // Other names for the same wires on the sheet: Fun[5:0] = INSTRUCTION[5:0]; Imm16[15:0] = INSTRUCTION[15:0];
  //   shamt[4:0] = INSTRUCTION[10:6]; Rd[4:0] = INSTRUCTION[15:11]; Rt[4:0] = INSTRUCTION[20:16];
  //   Rs[4:0] = INSTRUCTION[25:21]; Op[5:0] = INSTRUCTION[31:26]; sw = MemWr

  // Notes on the sheet:
  //   Inputs
  //   Outputs
endmodule
