// Logisim project mem.circ as structural Verilog: 1 circuit, main circuit main
module main (
  input  [31:0] Data_Mem_Addr,
  input  [31:0] Data_Mem_In,
  input  ACCESS_BYTE,
  input  MEM_WRITE,
  input  CLOCK,
  output [31:0] Data_Mem_Out
);

  wire not_1_out;
  wire [7:0] multiplexer_1_out;
  wire [31:0] bit_extender_1_out, controlled_buffer_1_out, subtractor_1_out;

  Subtractor #(.width(32)) subtractor_1 (
    .a(Data_Mem_Addr), .b(32'h10010000), .out(subtractor_1_out));  // open: bin, bout
  assign controlled_buffer_1_out = MEM_WRITE ? Data_Mem_In : 32'bz;  // Controlled_Buffer controlled_buffer_1
  RAM #(.addrWidth(24), .dataWidth(32)) ram_1 (
    .addr(subtractor_1_out[25:2]), .data(controlled_buffer_1_out), .sel(1'b1), .clk(CLOCK), .ld(not_1_out),
    .clr(1'b0));
  not not_1 (not_1_out, MEM_WRITE);
  Multiplexer #(.select(2), .width(8)) multiplexer_1 (
    .in0(controlled_buffer_1_out[7:0]), .in1(controlled_buffer_1_out[15:8]),
    .in2(controlled_buffer_1_out[23:16]), .in3(controlled_buffer_1_out[31:24]), .out(multiplexer_1_out),
    .sel(subtractor_1_out[1:0]));  // open: en
  assign bit_extender_1_out = {{24{1'b0}}, multiplexer_1_out};  // Bit_Extender bit_extender_1
  Multiplexer #(.width(32)) multiplexer_2 (
    .in0(controlled_buffer_1_out), .in1(bit_extender_1_out), .out(Data_Mem_Out), .sel(ACCESS_BYTE));  // open: en

  // Other names for the same wires on the sheet: accessByte = ACCESS_BYTE; memWrite = MEM_WRITE

  // Notes on the sheet:
  //   These are INPUTS to the circuit
  //   These are INPUTS to the circuit
  //   DO NOT CHANGE THE LOCATIONS OF THE INPUTS/OUTPUTS! IF YOU DO SO, YOU NEED TO MAKE SURE THE PINS ARE AT THE RIGHT PLACE!
  //   Yet again, the clock is not an actual clock, but an input, one that will be driven from a higher circuit
  //   lw case
  //   lb case
  //   zero extend it and handle everything else in cpu
  //   This is an OUTPUT to the circuit
endmodule
